# Fritzing sketch Semaforo (saved by Fritzing 0.8.7b)
breadboards: 1

parts:
  LED1 = LED - 5mm [color="Green (555nm)" package="5 mm [THT]"]
  LED2 = LED - 5mm [color="Yellow (595nm)" package="5 mm [THT]"]
  LED3 = LED - 5mm [color="Red (633nm)" package="5 mm [THT]"]
  LED4 = LED - 5mm [color="Red (633nm)" package="5 mm [THT]"]
  LED5 = LED - 5mm [color="Yellow (595nm)" package="5 mm [THT]"]
  LED6 = LED - 5mm [color="Green (555nm)" package="5 mm [THT]"]
  LED7 = LED - 5mm [color="Green (555nm)" package="5 mm [THT]"]
  LED8 = LED - 5mm [color="Red (633nm)" package="5 mm [THT]"]
  LED9 = LED - 5mm [color="Yellow (595nm)" package="5 mm [THT]"]
  Componente1 = Arduino Uno (Rev3)
  S1 = Pushbutton [package="[THT]"]
  S2 = Pushbutton [package="[THT]"]
  S3 = Pushbutton [package="[THT]"]
  R1 = Resistor [tolerance=±5% resistance=220 package=THT]

nets:
  N1: LED1.cathode, LED2.cathode, LED3.cathode, LED4.cathode, LED5.cathode, LED6.cathode, LED7.cathode, LED8.cathode, LED9.cathode, Componente1.GND
  N2: LED1.anode, Componente1.D11_PWM/MOSI
  N3: LED2.anode, Componente1.D12/MISO
  N4: LED3.anode, Componente1.D13/SCK
  N5: LED4.anode, Componente1.D7
  N6: LED5.anode, Componente1.D6_PWM
  N7: LED6.anode, Componente1.D5_PWM
  N8: LED7.anode, Componente1.D8
  N9: LED8.anode, Componente1.D10_PWM/SS
  N10: LED9.anode, Componente1.D9_PWM
  N11: Componente1.5V, S1.Pin_3, S1.Pin_4, S2.Pin_3, S2.Pin_4, S3.Pin_3, S3.Pin_4
  N12: S1.Pin_1, S1.Pin_2, R1.Pin_0
  N13: S2.Pin_1, S2.Pin_2
  N14: S3.Pin_1, S3.Pin_2
